# Fritzing sketch HubSensorUmidadeSolo (saved by Fritzing 0.9.3b)

parts:
  U1 = NodeMCU V1.0
  Componente1 = JeePlug experimenter's board
  Componente2 = JeePlug experimenter's board
  Componente3 = JeePlug experimenter's board
  Componente4 = JeePlug experimenter's board
  Componente5 = FC-28 Soil Hygrometer Module
  Componente6 = FC-28 Soil Hygrometer Module
  Componente7 = FC-28 Soil Hygrometer Module
  Componente8 = FC-28 Soil Hygrometer Module
  Componente9 = JeePlug experimenter's board
  Componente10 = JeePlug experimenter's board
  Componente11 = JeePlug experimenter's board
  Componente12 = JeePlug experimenter's board
  U2 = NodeMCU V1.0
  Componente13 = FC-28 Soil Hygrometer Module
  Componente14 = FC-28 Soil Hygrometer Module
  Componente15 = FC-28 Soil Hygrometer Module
  Componente16 = FC-28 Soil Hygrometer Module

nets:
  N1: U1.D0, Componente3.A1
  N2: U1.D1, Componente3.A2
  N3: U1.D2, Componente3.A3
  N4: U1.D3, Componente3.A4
  N5: U1.D4, Componente3.A5
  N6: U1.3V3, Componente3.A6, Componente4.B3, Componente4.N$26
  N7: U1.GND, Componente3.N$26, Componente4.B2, Componente4.B6, Componente4.A6
  N8: U1.D5, Componente4.N$24
  N9: U1.D6, Componente4.A1
  N10: U1.D7, Componente4.A2
  N11: U1.D8, Componente4.A3
  N12: U1.RX, Componente4.A4
  N13: U1.TX, Componente4.A5
  N14: U1.Vin, Componente4.N$8
  N15: U1.RST, Componente4.B5
  N16: U1.EN, Componente4.B4
  N17: U1.CLK, Componente4.B1
  N18: U1.SD0, Componente4.N$9
  N19: U1.CMD, Componente3.N$8
  N20: U1.SD1, Componente3.B6
  N21: U1.SD2, Componente3.B5
  N22: U1.SD3, Componente3.B4
  N23: U1.RSV#40, Componente3.B3
  N24: U1.RSV#41, Componente3.B2
  N25: U1.A0, Componente3.B1
  N26: Componente1.N$28, Componente8.GND
  N27: Componente1.N$29, Componente6.GND
  N28: Componente1.N$30, Componente2.N$27
  N29: Componente1.N$41, Componente8.VCC
  N30: Componente1.N$44, Componente2.N$41, Componente6.VCC
  N31: Componente2.N$29, Componente7.GND
  N32: Componente2.N$30, Componente5.GND
  N33: Componente2.N$42, Componente7.VCC
  N34: Componente2.N$46, Componente5.VCC
  N35: Componente9.N$27, Componente11.N$26, Componente12.B2, Componente12.B6, Componente12.A6, Componente12.N$63, U2.GND
  N36: Componente9.N$29, Componente14.GND
  N37: Componente9.N$30, Componente13.GND
  N38: Componente9.N$41, Componente12.N$8, Componente12.N$45, U2.Vin
  N39: Componente9.N$42, Componente14.VCC
  N40: Componente9.N$46, Componente13.VCC
  N41: Componente10.N$28, Componente15.GND
  N42: Componente10.N$29, Componente16.GND
  N43: Componente10.N$41, Componente15.VCC
  N44: Componente10.N$44, Componente16.VCC
  N45: Componente11.B6, U2.SD1
  N46: Componente11.B5, U2.SD2
  N47: Componente11.B4, U2.SD3
  N48: Componente11.B3, U2.RSV#40
  N49: Componente11.B2, U2.RSV#41
  N50: Componente11.B1, U2.A0
  N51: Componente11.A1, U2.D0
  N52: Componente11.A2, U2.D1
  N53: Componente11.A3, U2.D2
  N54: Componente11.A4, U2.D3
  N55: Componente11.A5, U2.D4
  N56: Componente11.A6, Componente12.B3, Componente12.N$26, U2.3V3
  N57: Componente11.N$8, U2.CMD
  N58: Componente12.B5, U2.RST
  N59: Componente12.B4, U2.EN
  N60: Componente12.B1, U2.CLK
  N61: Componente12.A1, U2.D6
  N62: Componente12.A2, U2.D7
  N63: Componente12.A3, U2.D8
  N64: Componente12.A4, U2.RX
  N65: Componente12.A5, U2.TX
  N66: Componente12.N$9, U2.SD0
  N67: Componente12.N$24, U2.D5

custom parts:
  NodeMCU V1.0: ESP8266 based NodeMCU
  FC-28 Soil Hygrometer Module: The FC-28 is a soil hygrometer module that uses the Texas Instruments LM393 comparator chip to provide an analog measurement of soil humidity. The digital output is high when soil moisture is over a certain threshold, as determined by adjusting the potentiometer.
