# Fritzing sketch V1SensorUmidadeSolo (saved by Fritzing 0.9.3b)

parts:
  U1 = NodeMCU V1.0
  Componente2 = FC-28 Soil Hygrometer Module
  Componente7 = FC-28 Soil Hygrometer Module - Probe
  Componente8 = JeePlug experimenter's board
  Componente9 = JeePlug experimenter's board
  Componente10 = JeePlug experimenter's board
  Componente11 = JeePlug experimenter's board
  Componente12 = FC-28 Soil Hygrometer Module - Probe
  U2 = NodeMCU V1.0
  J1 = Screw terminal - 2 pins [package=THT]
  Componente1 = JeePlug experimenter's board
  Componente4 = JeePlug experimenter's board
  Componente5 = JeePlug experimenter's board
  Componente6 = JeePlug experimenter's board
  J2 = Screw terminal - 2 pins [package=THT]

nets:
  N1: U1.D0, Componente4.B6
  N2: U1.D1, Componente4.B5
  N3: U1.D2, Componente4.B4
  N4: U1.D3, Componente4.B3
  N5: U1.D4, Componente4.B2
  N6: U1.3V3, Componente1.A4, Componente1.N$9, Componente4.B1
  N7: U1.GND, Componente1.B1, Componente1.A1, Componente1.A5, Componente4.N$9
  N8: U1.D5, Componente1.N$8
  N9: U1.D6, Componente1.B6
  N10: U1.D7, Componente1.B5
  N11: U1.D8, Componente1.B4
  N12: U1.RX, Componente1.B3
  N13: U1.TX, Componente1.B2
  N14: U1.Vin, Componente1.N$24
  N15: U1.RST, Componente1.A2
  N16: U1.EN, Componente1.A3
  N17: U1.CLK, Componente1.A6
  N18: U1.SD0, Componente1.N$26
  N19: U1.CMD, Componente4.N$24
  N20: U1.SD1, Componente4.A1
  N21: U1.SD2, Componente4.A2
  N22: U1.SD3, Componente4.A3
  N23: U1.RSV#40, Componente4.A4
  N24: U1.RSV#41, Componente4.A5
  N25: U1.A0, Componente4.A6
  N26: Componente2.VCC, Componente8.N$40
  N27: Componente2.GND, Componente8.N$41
  N28: Componente2.AO, Componente9.N$26, U2.A0
  N29: Componente2.POS, Componente11.N$20, Componente12.POS
  N30: Componente2.NEG, Componente11.N$30, Componente11.N$36, Componente12.NEG
  N31: Componente7.POS, Componente6.N$30
  N32: Componente7.NEG, Componente6.N$36
  N33: Componente8.B2, Componente8.A2, Componente8.A6, Componente9.B1, U2.GND
  N34: Componente8.B1, Componente8.A5, Componente9.B2, U2.3V3
  N35: Componente8.B6, U2.D7
  N36: Componente8.B5, U2.D8
  N37: Componente8.B4, U2.RX
  N38: Componente8.B3, U2.TX
  N39: Componente8.A1, Componente10.N$26, U2.Vin, J1.pin2
  N40: Componente8.A3, U2.RST
  N41: Componente8.A4, U2.EN
  N42: Componente8.N$8, U2.D6
  N43: Componente8.N$26, U2.CLK
  N44: Componente8.N$49, Componente10.A6, J1.pin1
  N45: Componente9.B3, U2.D4
  N46: Componente9.B6, U2.D1
  N47: Componente9.B5, U2.D2
  N48: Componente9.B4, U2.D3
  N49: Componente9.A1, U2.CMD
  N50: Componente9.A2, U2.SD1
  N51: Componente9.A3, U2.SD2
  N52: Componente9.A4, U2.SD3
  N53: Componente9.A5, U2.RSV#40
  N54: Componente9.A6, U2.RSV#41
  N55: Componente9.N$8, U2.D0
  N56: Componente9.N$9, U2.D5
  N57: Componente9.N$24, U2.SD0
  N58: Componente5.A5, J2.pin1
  N59: Componente5.A6, J2.pin2

custom parts:
  NodeMCU V1.0: ESP8266 based NodeMCU
  FC-28 Soil Hygrometer Module: The FC-28 is a soil hygrometer module that uses the Texas Instruments LM393 comparator chip to provide an analog measurement of soil humidity. The digital output is high when soil moisture is over a certain threshold, as determined by adjusting the potentiometer.
  FC-28 Soil Hygrometer Module - Probe: The FC-28 is a soil hygrometer module that uses the Texas Instruments LM393 comparator chip to provide an analog measurement of soil humidity.
